// Logisim project p3.circ as structural Verilog: 10 circuits, main circuit main
module main (
  input  rst,
  output [31:0] out_2,
  output [31:0] out_3,
  output out_4,
  output [4:0] out_5,
  output [31:0] out_6,
  output out_7,
  output [31:0] out_8,
  output [31:0] out_9
);

  wire ALUScr, clk, cu_and_1_add, cu_and_1_beq, cu_and_1_jal, cu_and_1_jr, cu_and_1_lui, cu_and_1_lw,
       cu_and_1_ori, cu_and_1_sub, cu_and_1_sw, EXTOp, Jzero;
  wire [1:0] MemToReg, RegDst;
  wire [2:0] branch;
  wire [3:0] ALUOp;
  wire [4:0] rd, rs, rt;
  wire [5:0] func, Op;
  wire [15:0] imm16;
  wire [25:0] imm26;
  wire [31:0] bit_extender_1_out, bit_extender_2_out, multiplexer_3_out, multiplexer_4_out, npc_1_npc, PC_4,
       ReadData, ReadData1;

  Clock clock_1 (.out(clk));
  NPC npc_1 (
    .PC(out_3), .Jzero(Jzero), .imm26(imm26), .RA(ReadData1), .Branch(branch), .PC___4(PC_4),
    .NPC(npc_1_npc), .imm16(imm16));
  PC pc_1 (.NPC(npc_1_npc), .NowPC(out_3), .clk(clk), .rst(rst));
  IM im_1 (.PC(out_3), .OP(out_2));
  Splitter splitter_1 (
    .OP(out_2), .Op_31_26(Op), .rs_25_21(rs), .rt_20_16(rt), .rd_15_11(rd), .func_5_0(func),
    .imm16_15_0(imm16), .imm26_25_0(imm26));
  CU_and cu_and_1 (
    .func(func), .op(Op), .add(cu_and_1_add), .sub(cu_and_1_sub), .ori(cu_and_1_ori), .lw(cu_and_1_lw),
    .sw(cu_and_1_sw), .beq(cu_and_1_beq), .lui(cu_and_1_lui), .jal(cu_and_1_jal), .jr(cu_and_1_jr));
  CU_or cu_or_1 (
    .add(cu_and_1_add), .ALUScr(ALUScr), .RegWrite(out_4), .MemWrite(out_7), .EXTOp(EXTOp), .ALUop(ALUOp),
    .Branch(branch), .RegDst(RegDst), .MemToReg(MemToReg), .sub(cu_and_1_sub), .ori(cu_and_1_ori),
    .lw(cu_and_1_lw), .sw(cu_and_1_sw), .beq(cu_and_1_beq), .lui(cu_and_1_lui), .jar(cu_and_1_jal),
    .jr(cu_and_1_jr));
  Multiplexer #(.select(2), .width(5)) multiplexer_1 (
    .in0(rt), .in1(rd), .in2({5{1'b1}}), .out(out_5), .sel(RegDst));  // open: in3, en
  Multiplexer #(.select(2), .width(32)) multiplexer_2 (
    .in0(out_8), .in1(ReadData), .in2(PC_4), .out(out_6), .sel(MemToReg));  // open: in3, en
  GRF grf_1 (
    .in_1(clk), .in_2(rst), .in_3(out_4), .in_4(rs), .in_5(rt), .in_6(out_5), .in_7(out_6), .RD1(ReadData1),
    .RD2(out_9));
  assign bit_extender_1_out = {{16{1'b0}}, imm16};  // Bit_Extender bit_extender_1
  assign bit_extender_2_out = {{16{imm16[15]}}, imm16};  // Bit_Extender bit_extender_2
  Multiplexer #(.width(32)) multiplexer_3 (
    .in0(bit_extender_1_out), .in1(bit_extender_2_out), .out(multiplexer_3_out), .sel(EXTOp));  // open: en
  Multiplexer #(.width(32)) multiplexer_4 (
    .in0(out_9), .in1(multiplexer_3_out), .out(multiplexer_4_out), .sel(ALUScr));  // open: en
  ALU alu_1 (.ALUOp(ALUOp), .a(ReadData1), .b(multiplexer_4_out), .result(out_8), .jZero(Jzero));
  DM dm_1 (
    .DMOp(2'b00), .addr(out_8), .memWrite(out_7), .clk(clk), .reset(rst), .writeData(out_9),
    .ReadData(ReadData));

  // Other names for the same wires on the sheet: Instr[31:0] = out_2; ALUResult[31:0] = out_8; MemAddr[31:0] = out_8;
  //   MemWrite = out_7; pc[31:0] = out_3; MemData[31:0] = out_9; ReadData2[31:0] = out_9; RegAddr[4:0] = out_5;
  //   RegData[31:0] = out_6; RegWrite = out_4
endmodule

module ALU (
  input  [3:0] ALUOp,
  input  [31:0] a,
  input  [31:0] b,
  output jZero,
  output [31:0] result
);

  wire [31:0] adder_1_out, and_1_out, or_1_out, subtractor_1_out;

  Adder #(.width(32)) adder_1 (.a(a), .b(b), .out(adder_1_out));  // open: cin, cout
  Subtractor #(.width(32)) subtractor_1 (.a(a), .b(b), .out(subtractor_1_out));  // open: bin, bout
  assign or_1_out = a | b;  // OR_Gate or_1, 32 bits wide
  assign and_1_out = a & b;  // AND_Gate and_1, 32 bits wide
  Multiplexer #(.select(4), .width(32)) multiplexer_1 (
    .in0(adder_1_out), .in1(subtractor_1_out), .in2(or_1_out), .in3(and_1_out), .in4({b[15:0], {16{1'b0}}}),
    .out(result), .sel(ALUOp));  // open: in5, in6, in7, in8, in9, in10, in11, in12, in13, in14, in15, en
  Comparator #(.width(32)) comparator_1 (.a({32{1'b0}}), .b(result), .eq(jZero));  // open: gt, lt
endmodule

module IM (
  input  [31:0] PC,
  output [31:0] OP
);

  wire [31:0] subtractor_1_out;

  Subtractor #(.width(32)) subtractor_1 (.a(PC), .b(32'h3000), .out(subtractor_1_out));  // open: bin, bout
  ROM #(.addrWidth(12), .dataWidth(32)) rom_1 (.addr(subtractor_1_out[13:2]), .data(OP));  // open: sel

  // Notes on the sheet:
  //   contents of rom_1 (hex, n*v repeats v):
  //   341c0000 341d0000 34013456 210820 8c010004 ac010004 3c027878 411822 3c051234 34040005 0 ac85ffff
  //   8c83ffff 10650001 1000000d 34670404 10e3000b 0 3c087777 3508ffff 80022 34001100 e65020 34080000
  //   34090001 340a0001 10a4020 1109fffe 1000ffff
endmodule

module GRF (
  input  in_1,
  input  in_2,
  input  in_3,
  input  [4:0] in_4,
  input  [4:0] in_5,
  input  [4:0] in_6,
  input  [31:0] in_7,
  output [31:0] RD1,
  output [31:0] RD2
);

  wire [31:0] _0, S0, S1in, S1out, S2in, S2out, S3in, S3out, S4in, S4out, S5in, S5out, S6in, S6out, S7in,
       S7out, S8in, S8out, S9in, S9out, S10in, S10out, S11in, S11out, S12in, S12out, S13in, S13out, S14in,
       S14out, S15in, S15out, S16in, S16out, S17in, S17out, S18in, S18out, S19in, S19out, S20in, S20out,
       S21in, S21out, S22in, S22out, S23in, S23out, S24in, S24out, S25in, S25out, S26in, S26out, S27in,
       S27out, S28in, S28out, S29in, S29out, S30in, S30out, S31in, S31out;

  Multiplexer #(.select(5), .width(32)) multiplexer_1 (
    .in0({32{1'b0}}), .in1(S1out), .in2(S2out), .in3(S3out), .in4(S4out), .in5(S5out), .in6(S6out),
    .in7(S7out), .in8(S8out), .in9(S9out), .in10(S10out), .in11(S11out), .in12(S12out), .in13(S13out),
    .in14(S14out), .in15(S15out), .in16(S16out), .in17(S17out), .in18(S18out), .in19(S19out), .in20(S20out),
    .in21(S21out), .in22(S22out), .in23(S23out), .in24(S24out), .in25(S25out), .in26(S26out), .in27(S27out),
    .in28(S28out), .in29(S29out), .in30(S30out), .in31(S31out), .out(RD1), .sel(in_4));  // open: en
  Multiplexer #(.select(5), .width(32)) multiplexer_2 (
    .in0({32{1'b0}}), .in1(S1out), .in2(S2out), .in3(S3out), .in4(S4out), .in5(S5out), .in6(S6out),
    .in7(S7out), .in8(S8out), .in9(S9out), .in10(S10out), .in11(S11out), .in12(S12out), .in13(S13out),
    .in14(S14out), .in15(S15out), .in16(S16out), .in17(S17out), .in18(S18out), .in19(S19out), .in20(S20out),
    .in21(S21out), .in22(S22out), .in23(S23out), .in24(S24out), .in25(S25out), .in26(S26out), .in27(S27out),
    .in28(S28out), .in29(S29out), .in30(S30out), .in31(S31out), .out(RD2), .sel(in_5));  // open: en
  Demultiplexer #(.select(5), .width(32), .tristate("true")) demultiplexer_1 (
    .out0(_0), .out1(S1in), .out2(S2in), .out3(S3in), .out4(S4in), .out5(S5in), .out6(S6in), .out7(S7in),
    .out8(S8in), .out9(S9in), .out10(S10in), .out11(S11in), .out12(S12in), .out13(S13in), .out14(S14in),
    .out15(S15in), .out16(S16in), .out17(S17in), .out18(S18in), .out19(S19in), .out20(S20in), .out21(S21in),
    .out22(S22in), .out23(S23in), .out24(S24in), .out25(S25in), .out26(S26in), .out27(S27in), .out28(S28in),
    .out29(S29in), .out30(S30in), .out31(S31in), .in(in_7), .sel(in_6), .en(in_3));
  Register #(.width(32)) u_S0 (.D(_0), .en(in_3), .Q(S0), .clk(in_1), .clr(in_2));
  Register #(.width(32)) S4 (.D(S4in), .en(in_3), .Q(S4out), .clk(in_1), .clr(in_2));
  Register #(.width(32)) S8 (.D(S8in), .en(in_3), .Q(S8out), .clk(in_1), .clr(in_2));
  Register #(.width(32)) S12 (.D(S12in), .en(in_3), .Q(S12out), .clk(in_1), .clr(in_2));
  Register #(.width(32)) S16 (.D(S16in), .en(in_3), .Q(S16out), .clk(in_1), .clr(in_2));
  Register #(.width(32)) S20 (.D(S20in), .en(in_3), .Q(S20out), .clk(in_1), .clr(in_2));
  Register #(.width(32)) S24 (.D(S24in), .en(in_3), .Q(S24out), .clk(in_1), .clr(in_2));
  Register #(.width(32)) S28 (.D(S28in), .en(in_3), .Q(S28out), .clk(in_1), .clr(in_2));
  Register #(.width(32)) S1 (.D(S1in), .en(in_3), .Q(S1out), .clk(in_1), .clr(in_2));
  Register #(.width(32)) S5 (.D(S5in), .en(in_3), .Q(S5out), .clk(in_1), .clr(in_2));
  Register #(.width(32)) S9 (.D(S9in), .en(in_3), .Q(S9out), .clk(in_1), .clr(in_2));
  Register #(.width(32)) S1_2 (.D(S13in), .en(in_3), .Q(S13out), .clk(in_1), .clr(in_2));
  Register #(.width(32)) S1_3 (.D(S17in), .en(in_3), .Q(S17out), .clk(in_1), .clr(in_2));
  Register #(.width(32)) S21 (.D(S21in), .en(in_3), .Q(S21out), .clk(in_1), .clr(in_2));
  Register #(.width(32)) S25 (.D(S25in), .en(in_3), .Q(S25out), .clk(in_1), .clr(in_2));
  Register #(.width(32)) S29 (.D(S29in), .en(in_3), .Q(S29out), .clk(in_1), .clr(in_2));
  Register #(.width(32)) S2 (.D(S2in), .en(in_3), .Q(S2out), .clk(in_1), .clr(in_2));
  Register #(.width(32)) S6 (.D(S6in), .en(in_3), .Q(S6out), .clk(in_1), .clr(in_2));
  Register #(.width(32)) S10 (.D(S10in), .en(in_3), .Q(S10out), .clk(in_1), .clr(in_2));
  Register #(.width(32)) S14 (.D(S14in), .en(in_3), .Q(S14out), .clk(in_1), .clr(in_2));
  Register #(.width(32)) S18 (.D(S18in), .en(in_3), .Q(S18out), .clk(in_1), .clr(in_2));
  Register #(.width(32)) S22 (.D(S22in), .en(in_3), .Q(S22out), .clk(in_1), .clr(in_2));
  Register #(.width(32)) S26 (.D(S26in), .en(in_3), .Q(S26out), .clk(in_1), .clr(in_2));
  Register #(.width(32)) S30 (.D(S30in), .en(in_3), .Q(S30out), .clk(in_1), .clr(in_2));
  Register #(.width(32)) S23 (.D(S23in), .en(in_3), .Q(S23out), .clk(in_1), .clr(in_2));
  Register #(.width(32)) S27 (.D(S27in), .en(in_3), .Q(S27out), .clk(in_1), .clr(in_2));
  Register #(.width(32)) S31 (.D(S31in), .en(in_3), .Q(S31out), .clk(in_1), .clr(in_2));
  Register #(.width(32)) S3 (.D(S3in), .en(in_3), .Q(S3out), .clk(in_1), .clr(in_2));
  Register #(.width(32)) S7 (.D(S7in), .en(in_3), .Q(S7out), .clk(in_1), .clr(in_2));
  Register #(.width(32)) S11 (.D(S11in), .en(in_3), .Q(S11out), .clk(in_1), .clr(in_2));
  Register #(.width(32)) S15 (.D(S15in), .en(in_3), .Q(S15out), .clk(in_1), .clr(in_2));
  Register #(.width(32)) S19 (.D(S19in), .en(in_3), .Q(S19out), .clk(in_1), .clr(in_2));

  // Other names for the same wires on the sheet: A1[4:0] = in_4; A2[4:0] = in_5; clk = in_1; reset = in_2;
  //   WD[31:0] = in_7; WE = in_3; WriteRegAddr[4:0] = in_6
endmodule

module DM (
  input  [1:0] DMOp,
  input  [31:0] addr,
  input  memWrite,
  input  clk,
  input  reset,
  input  [31:0] writeData,
  output [31:0] ReadData
);

  wire decoder_1_out0, decoder_1_out1, decoder_1_out2, decoder_1_out3, decoder_2_out0, decoder_2_out1;
  wire [7:0] B1, B2, B3, B4, multiplexer_1_out, multiplexer_2_out, multiplexer_3_out, multiplexer_4_out,
       multiplexer_8_out;
  wire [15:0] multiplexer_5_out, multiplexer_6_out, multiplexer_9_out;
  wire [31:0] bit_extender_1_out, bit_extender_2_out, multiplexer_7_out;

  Decoder #(.select(2)) decoder_1 (
    .out0(decoder_1_out0), .out1(decoder_1_out1), .out2(decoder_1_out2), .out3(decoder_1_out3),
    .sel(addr[1:0]));  // open: en
  Decoder decoder_2 (.out0(decoder_2_out0), .out1(decoder_2_out1), .sel(addr[1]));  // open: en
  Multiplexer #(.width(8)) multiplexer_1 (
    .in0(B1), .in1(writeData[7:0]), .out(multiplexer_1_out), .sel(decoder_1_out0));  // open: en
  Multiplexer #(.width(8)) multiplexer_2 (
    .in0(B2), .in1(writeData[7:0]), .out(multiplexer_2_out), .sel(decoder_1_out1));  // open: en
  Multiplexer #(.width(8)) multiplexer_3 (
    .in0(B3), .in1(writeData[7:0]), .out(multiplexer_3_out), .sel(decoder_1_out2));  // open: en
  Multiplexer #(.width(8)) multiplexer_4 (
    .in0(B4), .in1(writeData[7:0]), .out(multiplexer_4_out), .sel(decoder_1_out3));  // open: en
  Multiplexer #(.width(16)) multiplexer_5 (
    .in0({B2, B1}), .in1(writeData[15:0]), .out(multiplexer_5_out), .sel(decoder_2_out0));  // open: en
  Multiplexer #(.width(16)) multiplexer_6 (
    .in0({B4, B3}), .in1(writeData[15:0]), .out(multiplexer_6_out), .sel(decoder_2_out1));  // open: en
  Multiplexer #(.select(2), .width(32)) multiplexer_7 (
    .in0(writeData), .in1({multiplexer_4_out, multiplexer_3_out, multiplexer_2_out, multiplexer_1_out}),
    .in2({multiplexer_6_out, multiplexer_5_out}), .out(multiplexer_7_out), .sel(DMOp));  // open: in3, en
  Multiplexer #(.select(2), .width(8)) multiplexer_8 (
    .in0(B1), .in1(B2), .in2(B3), .in3(B4), .out(multiplexer_8_out), .sel(addr[1:0]));  // open: en
  assign bit_extender_1_out = {{24{multiplexer_8_out[7]}}, multiplexer_8_out};  // Bit_Extender bit_extender_1
  assign bit_extender_2_out = {{16{multiplexer_9_out[15]}}, multiplexer_9_out};  // Bit_Extender bit_extender_2
  Multiplexer #(.width(16)) multiplexer_9 (
    .in0({B2, B1}), .in1({B4, B3}), .out(multiplexer_9_out), .sel(addr[1]));  // open: en
  RAM #(.addrWidth(12), .dataWidth(32), .bus("separate")) ram_1 (
    .addr(addr[13:2]), .din(multiplexer_7_out), .data({B4, B3, B2, B1}), .str(memWrite), .clk(clk),
    .clr(reset));  // open: sel, ld
  Multiplexer #(.select(2), .width(32)) multiplexer_10 (
    .in0({B4, B3, B2, B1}), .in1(bit_extender_1_out), .in2(bit_extender_2_out), .out(ReadData), .sel(DMOp));  // open: in3, en
  // Probe on ReadData

  // Other names for the same wires on the sheet: opB[1:0] = addr[1:0]; opHw = addr[1]; Hw1[15:0] = {B2, B1};
  //   Hw2[15:0] = {B4, B3}; DataB[7:0] = writeData[7:0]; DataHw[15:0] = writeData[15:0]
endmodule

module CU_and (
  input  [5:0] func,
  input  [5:0] op,
  output add,
  output sub,
  output ori,
  output lw,
  output sw,
  output beq,
  output lui,
  output jal,
  output jr
);

  wire _000000_out, and_1_out, and_2_out, and_3_out, not_1_out, not_2_out, not_3_out, not_4_out, not_5_out,
       not_6_out, not_7_out, not_8_out, not_9_out, not_10_out, not_11_out, not_12_out;

  not not_1 (not_1_out, op[0]);
  not not_2 (not_2_out, op[2]);
  not not_3 (not_3_out, op[1]);
  not not_4 (not_4_out, op[3]);
  not not_5 (not_5_out, op[4]);
  not not_6 (not_6_out, op[5]);
  and _000000 (_000000_out, not_1_out, not_3_out, not_2_out, not_4_out, not_5_out, not_6_out);
  and _001101 (ori, not_6_out, not_5_out, op[3], op[2], not_3_out, op[0]);
  and _100011 (lw, op[5], not_5_out, not_4_out, not_2_out, op[1], op[0]);
  and _101011 (sw, op[5], not_5_out, op[3], not_2_out, op[1], op[0]);
  and _000100 (beq, not_6_out, not_5_out, not_4_out, op[2], not_3_out, not_1_out);
  and _001111 (lui, not_6_out, not_5_out, op[3], op[2], op[1], op[0]);
  and _000011 (jal, not_6_out, not_5_out, not_4_out, not_2_out, op[1], op[0]);
  not not_7 (not_7_out, func[0]);
  not not_8 (not_8_out, func[1]);
  not not_9 (not_9_out, func[3]);
  not not_10 (not_10_out, func[2]);
  not not_11 (not_11_out, func[4]);
  not not_12 (not_12_out, func[5]);
  and and_1 (and_1_out, not_7_out, not_8_out, not_10_out, not_9_out, not_11_out, func[5]);
  and and_2 (and_2_out, func[5], not_11_out, not_9_out, not_10_out, func[1], not_7_out);
  and u_add (add, and_1_out, _000000_out);
  and u_sub (sub, and_2_out, _000000_out);
  and and_3 (and_3_out, not_12_out, not_11_out, func[3], not_10_out, not_8_out, not_7_out);
  and u_jr (jr, _000000_out, and_3_out);
endmodule

module CU_or (
  input  add,
  input  sub,
  input  ori,
  input  lw,
  input  sw,
  input  beq,
  input  lui,
  input  jar,
  input  jr,
  output [3:0] ALUop,
  output [2:0] Branch,
  output [1:0] RegDst,
  output [1:0] MemToReg,
  output ALUScr,
  output RegWrite,
  output MemWrite,
  output EXTOp
);

  or RegDst1 (RegDst[1], 1'b0, jar);
  or RegDst0 (RegDst[0], 1'b0, add, sub);
  or or_1 (ALUScr, 1'b0, ori, lw, sw, lui);
  buf MemToReg1 (MemToReg[1], 1'b0);  // OR_Gate
  or MemToReg0 (MemToReg[0], 1'b0, lw);
  or or_2 (RegWrite, 1'b0, add, sub, ori, lw, lui);
  or or_3 (MemWrite, 1'b0, sw);
  or or_4 (EXTOp, 1'b0, lw, sw, beq);
  buf ALU3 (ALUop[3], 1'b0);  // OR_Gate
  or ALU2 (ALUop[2], 1'b0, lui);
  or ALU1 (ALUop[1], 1'b0, ori);
  or ALU0 (ALUop[0], 1'b0, sub, beq);
  buf Branch2 (Branch[2], 1'b0);  // OR_Gate
  buf Branck1 (Branch[1], 1'b0);  // OR_Gate
  or Branch0 (Branch[0], 1'b0, beq);
endmodule

module NPC (
  input  [31:0] PC,
  input  Jzero,
  input  [15:0] imm16,
  input  [25:0] imm26,
  input  [31:0] RA,
  input  [2:0] Branch,
  output [31:0] PC___4,
  output [31:0] NPC
);

  wire [31:0] adder_2_out, bit_extender_1_out, multiplexer_1_out, shifter_1_out;

  assign bit_extender_1_out = {{16{imm16[15]}}, imm16};  // Bit_Extender bit_extender_1
  Adder #(.width(32)) adder_1 (.a(PC), .b(32'h4), .out(PC___4));  // open: cin, cout
  Shifter #(.width(32)) shifter_1 (.in(bit_extender_1_out), .\dist (5'b00010), .out(shifter_1_out));
  Adder #(.width(32)) adder_2 (.a(PC___4), .b(shifter_1_out), .out(adder_2_out));  // open: cin, cout
  Multiplexer #(.width(32)) multiplexer_1 (
    .in0(PC___4), .in1(adder_2_out), .out(multiplexer_1_out), .sel(Jzero));  // open: en
  Multiplexer #(.select(3), .width(32)) multiplexer_2 (
    .in0(PC___4), .in1(multiplexer_1_out), .in2({PC[31:28], imm26, 2'b00}), .in3(RA), .out(NPC), .sel(Branch));  // open: in4, in5, in6, in7, en
endmodule

module Splitter (
  input  [31:0] OP,
  output [5:0] Op_31_26,
  output [4:0] rs_25_21,
  output [4:0] rt_20_16,
  output [4:0] rd_15_11,
  output [5:0] func_5_0,
  output [15:0] imm16_15_0,
  output [25:0] imm26_25_0
);


  assign func_5_0 = OP[5:0];
  assign imm16_15_0 = OP[15:0];
  assign imm26_25_0 = OP[25:0];
  assign Op_31_26 = OP[31:26];
  assign rd_15_11 = OP[15:11];
  assign rs_25_21 = OP[25:21];
  assign rt_20_16 = OP[20:16];
endmodule

module PC (
  input  [31:0] NPC,
  input  clk,
  input  rst,
  output [31:0] NowPC
);

  wire [31:0] PC_q, xor_1_out;

  assign xor_1_out = NPC ^ 32'h3000;  // XOR_Gate xor_1, 32 bits wide
  Register #(.width(32)) PC (.D(xor_1_out), .Q(PC_q), .clk(clk), .clr(rst));  // open: en
  assign NowPC = 32'h3000 ^ PC_q;  // XOR_Gate xor_2, 32 bits wide
endmodule
